# Fritzing sketch KILO_MUX_SHIELD v1 (saved by Fritzing 0.9.1b)
circuit board: 13.1075cm x 6.21001cm
breadboards: 1

parts:
  U4 = IC, DIP package, 24 pins [chip_label=IC]
  J5 = shrouded pin header, 10 pins [form="♂ (shrouded male)"]
  J6 = shrouded pin header, 10 pins [form="♂ (shrouded male)"]
  J3 = shrouded pin header, 10 pins [form="♂ (shrouded male)"]
  J4 = shrouded pin header, 10 pins [form="♂ (shrouded male)"]
  U3 = IC, DIP package, 24 pins [chip_label=IC]
  U1 = 74HC595 [package="DIP16 [THT]"]
  U2 = 74HC595 [package="DIP16 [THT]"]
  J2 = shrouded pin header, 10 pins [form="♂ (shrouded male)"]
  J1 = shrouded pin header, 10 pins [form="♂ (shrouded male)"]
  Arduino_UNO = Arduino Uno (Rev3) - ICSP
  A5_A4_A3_A2 = female pin header, 4 pins [form="♀ (female)"]
  MIDI_OUT_-_IN = female pin header, 2 pins [form="♀ (female)"]
  RX_-_TX = female pin header, 2 pins [form="♀ (female)"]
  MIDI_OUT = Audio Jack (TRS) 3.5mm [package="4Ucon 08780 [THT]"]
  MIDI_IN = Audio Jack (TRS) 3.5mm [package="4Ucon 08780 [THT]"]
  6N138 = IC, DIP package, 8 pins [chip_label=IC]
  R20 = Resistor [tolerance=±5% resistance=220 package=THT]
  R1 = Resistor [tolerance=±5% resistance=220 package=THT]
  R2 = Resistor [tolerance=±5% resistance=1.8k package=THT]
  C4 = Ceramic Capacitor [capacitance=100nF package="200 mil [THT, multilayer]"]
  C3 = Ceramic Capacitor [capacitance=100nF package="100 mil [THT, multilayer]"]
  C2 = Ceramic Capacitor [capacitance=100nF package="100 mil [THT, multilayer]"]
  C1 = Ceramic Capacitor [capacitance=100nF package="100 mil [THT, multilayer]"]
  D2_D3 = female pin header, 2 pins [form="♀ (female)"]
  R3 = Resistor [tolerance=±5% resistance=220 package=THT]
  Sensor_Ultrasónico_HC-SR04 = female pin header, 4 pins [form="♀ (female)"]
  D1 = Diode [package=diode-1n4148]

nets:
  MUXB: U4.pin1, Arduino_UNO.A1
  N1: U4.pin2, J5.pin9
  N2: U4.pin3, J5.pin8
  N3: U4.pin4, J5.pin7
  N4: U4.pin5, J5.pin6
  N5: U4.pin6, J5.pin5
  N6: U4.pin7, J5.pin4
  N7: U4.pin8, J5.pin3
  N8: U4.pin9, J5.pin2
  S0: U4.pin10, U3.pin10, Arduino_UNO.D4
  S1: U4.pin11, U3.pin11, Arduino_UNO.D5_PWM
  GND: U4.pin12, U4.pin15, J5.pin1, J6.pin1, J3.pin1, J4.pin1, U3.pin12, U3.pin15, U1.GND, U1.OE, U2.GND, U2.OE, J2.pin6, J1.pin6, Arduino_UNO.GND, MIDI_OUT.Sleeve, MIDI_IN.Sleeve, 6N138.pin5, C4.0, C3.0, C2.0, C1.0, Sensor_Ultrasónico_HC-SR04.pin4
  S3: U4.pin13, U3.pin13, Arduino_UNO.D7
  S2: U4.pin14, U3.pin14, Arduino_UNO.D6_PWM
  N9: U4.pin16, J6.pin9
  N10: U4.pin17, J6.pin8
  N11: U4.pin18, J6.pin7
  N12: U4.pin19, J6.pin6
  N13: U4.pin20, J6.pin5
  N14: U4.pin21, J6.pin4
  N15: U4.pin22, J6.pin3
  N16: U4.pin23, J6.pin2
  5V: U4.pin24, J5.pin10, J6.pin10, J3.pin10, J4.pin10, U3.pin24, U1.MR, U1.VCC, U2.MR, U2.VCC, Arduino_UNO.5V, 6N138.pin8, R2.Pin_0, C4.1, C3.1, C2.1, C1.1, R3.Pin_0, Sensor_Ultrasónico_HC-SR04.pin1
  N17: J3.pin2, U3.pin9
  N18: J3.pin3, U3.pin8
  N19: J3.pin4, U3.pin7
  N20: J3.pin5, U3.pin6
  N21: J3.pin6, U3.pin5
  N22: J3.pin7, U3.pin4
  N23: J3.pin8, U3.pin3
  N24: J3.pin9, U3.pin2
  N25: J4.pin2, U3.pin23
  N26: J4.pin3, U3.pin22
  N27: J4.pin4, U3.pin21
  N28: J4.pin5, U3.pin20
  N29: J4.pin6, U3.pin19
  N30: J4.pin7, U3.pin18
  N31: J4.pin8, U3.pin17
  N32: J4.pin9, U3.pin16
  MUXA: U3.pin1, Arduino_UNO.A0
  N33: U1.Q1, J2.pin3
  N34: U1.Q2, J2.pin2
  N35: U1.Q3, J2.pin1
  N36: U1.Q4, J2.pin10
  N37: U1.Q5, J2.pin9
  N38: U1.Q6, J2.pin8
  N39: U1.Q7, J2.pin7
  N40: U1.Q7', U2.DS
  SH_CP: U1.SH_CP, U2.SH_CP, Arduino_UNO.D10_PWM/SS
  ST_CP: U1.ST_CP, U2.ST_CP, Arduino_UNO.D9_PWM
  DS: U1.DS, Arduino_UNO.D8
  N41: U1.Q0, J2.pin4
  N42: U2.Q1, J1.pin3
  N43: U2.Q2, J1.pin2
  N44: U2.Q3, J1.pin1
  N45: U2.Q4, J1.pin10
  N46: U2.Q5, J1.pin9
  N47: U2.Q6, J1.pin8
  N48: U2.Q7, J1.pin7
  N49: U2.Q0, J1.pin4
  N50: Arduino_UNO.A2, A5_A4_A3_A2.pin4
  N51: Arduino_UNO.A3, A5_A4_A3_A2.pin3
  N52: Arduino_UNO.A4/SDA, A5_A4_A3_A2.pin2
  N53: Arduino_UNO.A5/SCL, A5_A4_A3_A2.pin1
  ECHO: Arduino_UNO.D12/MISO, Sensor_Ultrasónico_HC-SR04.pin3
  TRIGGER: Arduino_UNO.D13/SCK, Sensor_Ultrasónico_HC-SR04.pin2
  N54: Arduino_UNO.D0/RX, RX_-_TX.pin2
  N55: Arduino_UNO.D1/TX, RX_-_TX.pin1
  N56: Arduino_UNO.D2, D2_D3.pin1
  N57: Arduino_UNO.D3_PWM, D2_D3.pin2
  N58: MIDI_OUT_-_IN.pin1, R20.Pin_0
  N59: MIDI_OUT_-_IN.pin2, 6N138.pin6, R2.Pin_1
  N60: MIDI_OUT.Ring, R20.Pin_1
  N61: MIDI_OUT.Tip, R3.Pin_1
  N62: MIDI_IN.Ring, 6N138.pin3, D1.A
  N63: MIDI_IN.Tip, R1.Pin_0
  N64: 6N138.pin2, R1.Pin_1, D1.C

notes:
  (4067)
  A
  B
  C
  D
  (595)
  YTX
  ISP HEADER
  US
  KILO-MUX

// code stored in the sketch: Kilo_muxShield_v3_6.ino

/*
Autor: Franco Grassano - YAELTEX
---
INFORMACIÓN DE LICENCIA
Kilo Mux Shield por Yaeltex se distribuye bajo una licencia
Creative Commons Atribución-CompartirIgual 4.0 Internacional - http://creativecommons.org/licenses/by-sa/4.0/
----
Código para el manejo de los integrados 74HC595 tomado de http://bildr.org/2011/02/74HC595/
Librería de multiplexado tomada de http://mayhewlabs.com/products/mux-shield-2
Librería para el manejo del sensor de ultrasonido tomada de http://playground.arduino.cc/Code/NewPing

Este código fue desarrollado para el KILO MUX SHIELD desarrolado en conjunto por Yaeltex y el Laboratorio del Juguete, en Buenos Aires, Argentina, 
apuntando al desarrollo de controladores MIDI con arduino.
Está preparado para manejar 2 registros de desplazamiento 74HC595 conectados en cadena (16 salidas digitales en total),
y 2 multiplexores CD4067 de 16 canales cada uno (16 entradas analógicas, y 16 entradas digitales), pero es expandible en el
caso de utilizar hardware diferente. Para ello se modifican los "define" NUM_MUX, NUM_CANALES_MUX y NUM_595s. 
NOTA: Se modificó la librería MuxShield, para trabajar sólo con 1 o 2 multiplexores. Si se necesita usar más multiplexores, descargar la librería original.

Para las entradas analógicas, por cuestiones de ruido se recomienda usar potenciómetros o sensores con buena estabilidad, y con preferencia con valores 
cercanos o menores a 10 Kohm.

Agradecimientos:
  - Jorge Crowe
  - Lucas Leal
  - Dimitri Diakopoulos
*/

#include <NewPing.h>
#include <MIDI.h>
#include <midi_Defs.h>
#include <midi_Namespace.h>
#include <midi_Settings.h>
#include <MuxShield.h>
// Descomentar la próxima línea si el compilador no encuentra MIDI
// MIDI_CREATE_DEFAULT_INSTANCE();

// Comentar la siguiente linea si no se usa sensor de ultrasonido
#define CON_ULTRASONIDO

// Comentar una de las dos lineas siguientes para definir el tipo de comunicación
#define COMUNICACION_MIDI
#define COMUNICACION_SERIAL

void setup(); // Esto es para solucionar el bug que tiene Arduino al usar los #ifdef del preprocesador

#define NUM_MUX 2 // Número de multiplexores a direccionar
#define NUM_CANALES_MUX 16 // Número de canales en cada mux

#define MUX_A 0
#define MUX_B 1
#define MUX_A_ENTRADA A0 // Pin analógico por dónde se lee el MUX A
#define MUX_B_ENTRADA A1 // Pin analógico por dónde se lee el MUX B

// CAMBIAR SEGÚN APLICACIÓN
#define MUX_DIGITAL   MUX_B   
// CAMBIAR SEGÚN APLICACIÓN
#define MUX_ANALOGICO MUX_A 

#define ENTRADA_DIGITAL   MUX_B_ENTRADA // CAMBIAR SEGÚN APLICACIÓN - Multiplexor con entradas digitales
#define ENTRADA_ANALOGICA MUX_A_ENTRADA // CAMBIAR SEGÚN APLICACIÓN - Multiplexor con entradas analógicas

#define NUM_595s 2 // Número de integrados 74HC595
#define NUM_LEDS NUM_595s*8 // Número de LEDs en total, NO CAMBIAR

// Estos valores dependen de como están cableados los botones en el controlador
// FIJOS - NO TOCAR!!!
#define NOTA_0_HW  0
#define NOTA_1_HW  1
#define NOTA_2_HW  2
#define NOTA_3_HW  3
#define NOTA_4_HW  4
#define NOTA_5_HW  5
#define NOTA_6_HW  6
#define NOTA_7_HW  7
#define NOTA_8_HW  8
#define NOTA_9_HW  9
#define NOTA_10_HW 10
#define NOTA_11_HW 11
#define NOTA_12_HW 12
#define NOTA_13_HW 13
#define NOTA_14_HW 14
#define NOTA_15_HW 15

// Estos son los valores de notas que se quieren recibir en la aplicación DAW.
// AJUSTABLES SEGÚN APLICACIÓN
#define NOTA_0_MIDI  0
#define NOTA_1_MIDI  1
#define NOTA_2_MIDI  2  
#define NOTA_3_MIDI  3
#define NOTA_4_MIDI  4
#define NOTA_5_MIDI  5
#define NOTA_6_MIDI  6
#define NOTA_7_MIDI  7
#define NOTA_8_MIDI  8
#define NOTA_9_MIDI  9
#define NOTA_10_MIDI 10
#define NOTA_11_MIDI 11
#define NOTA_12_MIDI 12
#define NOTA_13_MIDI 13
#define NOTA_14_MIDI 14
#define NOTA_15_MIDI 15

// Estos valores dependen de como están cableadas las entradas analógicas en el controlador
// FIJOS - NO TOCAR!!!
#define CC_0_HW  0
#define CC_1_HW  1
#define CC_2_HW  2
#define CC_3_HW  3
#define CC_4_HW  4
#define CC_5_HW  5
#define CC_6_HW  6
#define CC_7_HW  7
#define CC_8_HW  8
#define CC_9_HW  9
#define CC_10_HW 10
#define CC_11_HW 11
#define CC_12_HW 12
#define CC_13_HW 13
#define CC_14_HW 14
#define CC_15_HW 15

// Estos son los valores de Control Change que se quieren recibir en la aplicación DAW.
// AJUSTABLES SEGÚN APLICACIÓN
#define CC_0_MIDI  0
#define CC_1_MIDI  1
#define CC_2_MIDI  2
#define CC_3_MIDI  3
#define CC_4_MIDI  4
#define CC_5_MIDI  5
#define CC_6_MIDI  6
#define CC_7_MIDI  7
#define CC_8_MIDI  8
#define CC_9_MIDI  9
#define CC_10_MIDI 10
#define CC_11_MIDI 11
#define CC_12_MIDI 12
#define CC_13_MIDI 13
#define CC_14_MIDI 14
#define CC_15_MIDI 15
// CC para el sensor ultrasónico - AJUSTABLE
#define CC_US_MIDI 16

// Estos son los identificadores de cada LED en hardware.
// FIJOS - NO TOCAR!!!
#define N_LED_HW_0 0
#define N_LED_HW_1 1
#define N_LED_HW_2 2
#define N_LED_HW_3 3
#define N_LED_HW_4 4
#define N_LED_HW_5 5
#define N_LED_HW_6 6
#define N_LED_HW_7 7
#define N_LED_HW_8 8
#define N_LED_HW_9 9
#define N_LED_HW_10 10
#define N_LED_HW_11 11
#define N_LED_HW_12 12
#define N_LED_HW_13 13
#define N_LED_HW_14 14
#define N_LED_HW_15 15

// Estos son los valores de notas a los que responde cada LED. Deben estar apareados los LEDs que sean indicadores de botones.
// AJUSTABLES SEGÚN APLICACIÓN
#define N_LED_MIDI_0 0
#define N_LED_MIDI_1 1
#define N_LED_MIDI_2 2
#define N_LED_MIDI_3 3
#define N_LED_MIDI_4 4
#define N_LED_MIDI_5 5
#define N_LED_MIDI_6 6
#define N_LED_MIDI_7 7
#define N_LED_MIDI_8 8
#define N_LED_MIDI_9 9
#define N_LED_MIDI_10 10
#define N_LED_MIDI_11 11
#define N_LED_MIDI_12 12
#define N_LED_MIDI_13 13
#define N_LED_MIDI_14 14
#define N_LED_MIDI_15 15

#define NOTE_ON   127
#define NOTE_OFF  0

#define CANAL_MIDI_NOTES  1                              // DEFINIR CANAL MIDI A UTILIZAR
#define CANAL_MIDI_CC     1                              // DEFINIR CANAL MIDI A UTILIZAR
#define CANAL_MIDI_LEDS   1                              // DEFINIR CANAL MIDI A UTILIZAR

#define UMBRAL_RUIDO        1                      // Ventana de ruido para las entradas analógicas. Si entrada < entrada+umbral o 
                                                   //                                                   entrada > entrada-umbral descarta la lectura.
#define INTERVALO_LEDS      300                    // Intervalo de intermitencia
#define VELOCITY_LIM_TITILA 64                     // Limite de velocity para definir parpadeo - 0            - APAGADO
                                                   //                                            1 a LIMITE   - TITILA
                                                   //                                            LIMITE a 127 - ENCENDIDO
                                                   
#ifdef CON_ULTRASONIDO                                                   
  // DEFINES PARA SENSOR ULTRASONICO                                                 
  // FIJOS - NO CAMBIAR!!!
  #define TRIGGER_PIN          13        // Pin de arduino conectado al pin de trigger del sensor
  #define ECHO_PIN             12        // Pin de arduino conectado al pin de echo del sensor.
  #define PIN_BOTON_ACT_US     2
  #define PIN_LED_ACT_US       3
  #define MAX_US               MAX_DISTANCIA*US_ROUNDTRIP_CM   // Maximo tiempo en microsegundos que dura el pulso en retornar
  #define MIN_US               MIN_DISTANCIA*US_ROUNDTRIP_CM   // Minimo tiempo en microsegundos que dura el pulso en retornar
  // AJUSTABLES
  #define MAX_DISTANCIA        45        // Maxima distancia que se desea medir (en centimetros). El sensor mide hasta 400-500cm.
  #define MIN_DISTANCIA        2         // Minima distancia que se desea medir (en centimetros). El sensor mide desde 1cm.
  #define DELAY_ULTRAS         15        // Delay entre dos pings de
  #define UMBRAL_DIFERENCIA_US 80 
  #define FILTRO_US            3
#endif

#define VELOCIDAD_SERIAL 115200                    // Velocidad de transferencia (bits/seg) de la comunicación serial

#ifdef CON_ULTRASONIDO 
NewPing sensorUS(TRIGGER_PIN, ECHO_PIN, MAX_DISTANCIA); // Instancia de NewPing para el sensor US.
int ccSensorValuePrev[FILTRO_US];
#endif

MuxShield muxShield;                               // Objeto de la clase MuxShield, para leer los multiplexores

// Variables para los registros de desplazamiento
const int dataPin = 8;                             // Pin de datos (DS) conectado al pin 14 del 74HC595
const int latchPin = 9;                            // Pin de latch (ST_CP) conectado al pin 12 del 74HC595
const int clockPin = 10;                           // Pin de clock (SH_CP) conectado al pin 11 del 74HC595
boolean registros[NUM_LEDS];                       // Estado de los LEDs (HIGH - 1 o LOW - 0)
boolean leds_que_titilan[NUM_LEDS];                // Si está en 1, el LED titila. Si está en 0, no titila

// Datos analógicos
byte velocity[NUM_MUX][NUM_CANALES_MUX];               // Variable de 1 byte que guarda la velocity actual de cada canal
byte velocityPrev[NUM_MUX][NUM_CANALES_MUX];           // Variable de 1 byte que guarda la velocity anterior de cada canal


// Contadores, flags
int mux, canal;                           // Contadores para recorrer los multiplexores
bool tiempo_on = 0;                       // Tiempo que llevan encendidos los leds, para el parpadeo
unsigned int anteriorMillis = 0;          // Variable para guardar ms

void setup() {
  // Setear pines de salida
  pinMode(latchPin, OUTPUT);
  pinMode(dataPin, OUTPUT);
  pinMode(clockPin, OUTPUT);
#ifdef CON_ULTRASONIDO 
  pinMode(PIN_LED_ACT_US, OUTPUT);         // LED indicador para el sensor de distancia
  pinMode(PIN_BOTON_ACT_US,INPUT_PULLUP);  // Botón de activación para el sensor de distancia
#endif  
                                                    
  pinMode(ENTRADA_DIGITAL, INPUT);                // Estas dos líneas setean el pin analógico que recibe las entradas digitales como pin digital y
  digitalWrite(ENTRADA_DIGITAL, HIGH);            // setea el resistor de Pull-Up en el mismo


  // Guardar cantidad de ms desde el encendido
  anteriorMillis = millis();

  for (mux = 0; mux < NUM_MUX; mux++) {                // Setear todos los velocity a 0
    for (canal = 0; canal < NUM_CANALES_MUX; canal++) {
      velocity[mux][canal] = 0;
      velocityPrev[mux][canal] = 0;
    }
  }
  // Prescalers para el ADC
  const unsigned char PS_16 = (1 << ADPS2);
  const unsigned char PS_32 = (1 << ADPS2) | (1 << ADPS0);
  const unsigned char PS_64 = (1 << ADPS2) | (1 << ADPS1);
  const unsigned char PS_128 = (1 << ADPS2) | (1 << ADPS1) | (1 << ADPS0);
  // Setear el prescaler (divisor de clock) del ADC
  ADCSRA &= ~PS_128;  // Poner a 0 los bits del registro seteados por la librería de Arduino
  // Elegimos uno de los prescalers:
  // PS_16 (1MHz o 50000 muestras/s) 
  // PS_32 (500KHz o 31250 muestras/s) 
  // PS_64 (250KHz o 16666 muestras/s)
  // PS_128 (125KHz o 8620 muestras/s)
  // Atmel sugiere mantener la frecuencia de operación del ADC entre 50Khz y 200Khz, advirtiendo que 
  // puede degradarse la resolución si se supera la misma
  ADCSRA |= PS_16;    // Setear el prescaler al valor elegido

  clearRegisters();                             // Se limpia el array registros (todos a LOW)
  writeRegisters();                             // Se envían los datos al 595

#ifdef COMUNICACION_MIDI
  MIDI.begin(MIDI_CHANNEL_OMNI); MIDI.turnThruOff();  // Se inicializa la comunicación MIDI.
                                                      // Por default, la librería de Arduino MIDI tiene el THRU en ON, y NO QUEREMOS ESO!
#elif defined(COMUNICACION_SERIAL)
  Serial.begin(VELOCIDAD_SERIAL);                  // Se inicializa la comunicación serial. Descomentar para usar con Hairless MID
#endif
}

void loop() {  
#ifdef COMUNICACION_MIDI
   leer_MIDI();
#elif defined(COMUNICACION_SERIAL)
  encender_leds_serial();
#endif  

  if (millis() - anteriorMillis > INTERVALO_LEDS)          // Si transcurrieron más de X ms desde la ultima actualización,
    titilarLeds();
  leerEntradas();
#ifdef CON_ULTRASONIDO  
  leerUltrasonico();
#endif  
}


// Esta función lee todas las entradas y almacena los valores de cada una en la matriz 'velocity'.
// Compara con los valores previos, almacenados en 'velocityPrev', y si cambian, envía una NoteOn o NoteOff (entradas digitales) o un ControlChange (entradas analógicas)
void leerEntradas(void) {
  static bool noteOn[NUM_CANALES_MUX] = {};
  for (mux = 0; mux < NUM_MUX; mux++) {                                           // Recorro el numero de multiplexores, definido al principio
    for (canal = 0; canal < NUM_CANALES_MUX; canal++) {                                // Recorro todos los canales de cada multiplexor
      // ENTRADAS ANALÓGICAS
      if (mux == MUX_ANALOGICO) {                                                 // Si es un potenciómetro/fader/sensor,
        // CÓDIGO PARA LECTURA DE ENTRADAS ANALÓGICAS /////////////////////////////////////////////////////////////////////
        unsigned int analogData = muxShield.analogReadMS(mux + 1, canal);            // Leer entradas analógicas 'muxShield.analogReadMS(N_MUX,N_CANAL)'
        velocity[mux][canal] = analogData >> 3;                                      // El valor leido va de 0-1023. Convertimos a 0-127, dividiendo por 8.
        
        if (esRuido(canal) == 0) {                                         // Si lo que leo no es ruido
          #ifdef COMUNICACION_MIDI
            enviarControlChangeMidi(canal);
          #elif defined(COMUNICACION_SERIAL)
            enviarControlChangeSerial(canal);
          #endif
        }
        else continue;
      }
      // FIN CÓDIGO PARA LECTURA DE ENTRADAS ANALÓGICAS /////////////////////////////////////////////////////////////////
      // ENTRADAS DIGITALES
      if (mux == MUX_DIGITAL) {                                                    // Si es un pulsador,
        // CÓDIGO PARA LECTURA DE ENTRADAS DIGITALES /////////////////////////////////////////////////////////////////////
        velocity[mux][canal] = muxShield.digitalReadMS(mux + 1, canal);               // Leer entradas analógicas 'muxShield.analogReadMS(N_MUX,N_CANAL)'
        
        if (velocity[mux][canal] != velocityPrev[mux][canal]) {                        // Me interesa la lectura, si cambió el estado del botón,
          if (!velocity[mux][canal] && !noteOn[canal]) {                               // Si leo 0 (botón accionado) 
            noteOn[canal] = 1;
            // Se envía NOTE ON
            #ifdef COMUNICACION_MIDI
              enviarNoteMidi(canal, NOTE_ON);
            #elif defined(COMUNICACION_SERIAL)
              enviarNoteSerial(canal, NOTE_ON);
            #endif
          }
          else if (noteOn[canal]) {
            noteOn[canal] = 0;
            #ifdef COMUNICACION_MIDI
              enviarNoteMidi(canal, NOTE_OFF);
            #elif defined(COMUNICACION_SERIAL)
              enviarNoteSerial(canal, NOTE_OFF);
            #endif
          }
        }
        // FIN CÓDIGO PARA LECTURA DE ENTRADAS DIGITALES /////////////////////////////////////////////////////////////////////
      }
      velocityPrev[mux][canal] = velocity[mux][canal];             // Almacenar velocidad actual como anterior
    }
  }
}

#ifdef CON_ULTRASONIDO
void leerUltrasonico(void){
  static unsigned int antMillisUltraSonico = 0;  // Variable usada para almacenar los milisegundos desde el último Ping al sensor
  static bool estadoBotonAnt = 1;                // Inicializo inactivo (entrada activa baja)
  static bool estadoBoton = 1;                   // Inicializo inactivo (entrada activa baja)
  static bool estadoLed = 0;                     // Inicializo inactivo (salida activa alta)
  static bool sensorActivado = 0;                // Inicializo inactivo (variable interna)
  static unsigned int indiceFiltro = 0;     
    
  int microSeg = 0;
  
  // Este codigo verifica si se presionó el botón y activa o desactiva el sensor cada vez que se presiona
  estadoBoton = digitalRead(PIN_BOTON_ACT_US);
  if(estadoBoton == LOW && estadoBotonAnt == HIGH){  // Si el botón previamente estaba en estado alto, y ahora esta en estado bajo, quiere decir que paso de estar no presionado a presionado (activo bajo)
    estadoBotonAnt = LOW;                            // Actualizo el estado previo
    sensorActivado = !sensorActivado;                // Activo o desactivo el sensor
    estadoLed = !estadoLed;                          // Cambio el estado del LED
    digitalWrite(PIN_LED_ACT_US, estadoLed);         // Y actualizo la salida
  }
  else if(estadoBoton == HIGH && estadoBotonAnt == LOW){  // Si el botón previamente estaba en estado bajo, y ahora esta en estado alto, quiere decir que paso de estar presionado a no presionado 
    estadoBotonAnt = HIGH;                           // Actualizo el estado previo
  } 
  
  if(sensorActivado){      // Si el sensor está activado
    if (millis()-antMillisUltraSonico > DELAY_ULTRAS){
      antMillisUltraSonico = millis();
      microSeg = sensorUS.ping(); // Send ping, get ping time in microseconds (uS).
      int ccSensorValue = map(constrain(microSeg, MIN_US, MAX_US), MIN_US, MAX_US, 0, 127);
      if(ccSensorValue != ccSensorValuePrev[indiceFiltro]){
        if(!ccSensorValue & ccSensorValuePrev[indiceFiltro] > 10){      // Este if no permite que si se saca la mano o se excede la distancia maxima, el valor vuelva a 0
          ccSensorValue =  ccSensorValuePrev[indiceFiltro];             // igualando el valor actual con el último valor anterior, si el nuevo valor es 0 y el anterior es mayor a 10
        }
        // FILTRO DE MEDIA MÓVIL VALORES DE ULTRASONIDO
        for(int i = 0; i < FILTRO_US; i++){                      
          ccSensorValue += ccSensorValuePrev[i];           // Suma al valor actual, los N (FILTRO_US) valores anteriores 
        }
        ccSensorValue /= FILTRO_US+1;                      // Divido por N+1
        ccSensorValuePrev[indiceFiltro++] = ccSensorValue; // Y actualizo el índice del buffer circular
        indiceFiltro %= FILTRO_US+1;
        // FIN FILTRADO ////////////////////////////////
        
        #ifdef COMUNICACION_MIDI
          MIDI.sendControlChange(CC_US_MIDI, ccSensorValue, CANAL_MIDI_CC);
        #elif defined(COMUNICACION_SERIAL)
          Serial.print("Sensor Ultrasonico CC: "); Serial.print(CC_US_MIDI); Serial.print("  Valor: "); Serial.println(ccSensorValue);
        #endif
      }
      else return;        
    }
  }
}
#endif

#ifdef COMUNICACION_MIDI
// Lee el canal midi, note y velocity, y actualiza el estado de los leds.
void leer_MIDI(void) {
  // COMENTAR PARA DEBUGGEAR CON SERIAL ///////////////////////////////////////////////////////////////////////
  if (MIDI.read(CANAL_MIDI_LEDS)) {         // ¿Llegó un mensaje MIDI?
    byte led_number = MIDI.getData1();  // Capturo la nota
    byte led_vel = MIDI.getData2();
    switch (MIDI.getType())                  // Identifica que tipo de mensaje llegó (NoteOff, NoteOn, AfterTouchPoly, ControlChange, ProgramChange, AfterTouchChannel, PitchBend, SystemExclusive)
    {
      case midi::NoteOn:                       // En caso que sea NoteOn,
        if (led_vel > VELOCITY_LIM_TITILA) {     // Si la velocity es un valor entre LIMITE y 127, el led no parpadea
          switch(led_number){
            case N_LED_MIDI_0:
              setLed_595(N_LED_HW_0, HIGH); leds_que_titilan[N_LED_HW_0] = 0; break;      // Encender el LED correspondiente y no dejar que titile
            case N_LED_MIDI_1:
              setLed_595(N_LED_HW_1, HIGH); leds_que_titilan[N_LED_HW_1] = 0; break;            
            case N_LED_MIDI_2:
              setLed_595(N_LED_HW_2, HIGH); leds_que_titilan[N_LED_HW_2] = 0; break;            
            case N_LED_MIDI_3:
              setLed_595(N_LED_HW_3, HIGH); leds_que_titilan[N_LED_HW_3] = 0; break;            
            case N_LED_MIDI_4:
              setLed_595(N_LED_HW_4, HIGH); leds_que_titilan[N_LED_HW_4] = 0; break;            
            case N_LED_MIDI_5:
              setLed_595(N_LED_HW_5, HIGH); leds_que_titilan[N_LED_HW_5] = 0; break;            
            case N_LED_MIDI_6:
              setLed_595(N_LED_HW_6, HIGH); leds_que_titilan[N_LED_HW_6] = 0; break;            
            case N_LED_MIDI_7:
              setLed_595(N_LED_HW_7, HIGH); leds_que_titilan[N_LED_HW_7] = 0; break;            
            case N_LED_MIDI_8:
              setLed_595(N_LED_HW_8, HIGH); leds_que_titilan[N_LED_HW_8] = 0; break;            
            case N_LED_MIDI_9:
              setLed_595(N_LED_HW_9, HIGH); leds_que_titilan[N_LED_HW_9] = 0; break;            
            case N_LED_MIDI_10:
              setLed_595(N_LED_HW_10, HIGH); leds_que_titilan[N_LED_HW_10] = 0; break;           
            case N_LED_MIDI_11:
              setLed_595(N_LED_HW_11, HIGH); leds_que_titilan[N_LED_HW_11] = 0; break;           
            case N_LED_MIDI_12:
              setLed_595(N_LED_HW_12, HIGH); leds_que_titilan[N_LED_HW_12] = 0; break;           
            case N_LED_MIDI_13:
              setLed_595(N_LED_HW_13, HIGH); leds_que_titilan[N_LED_HW_13] = 0; break;           
            case N_LED_MIDI_14:
              setLed_595(N_LED_HW_14, HIGH); leds_que_titilan[N_LED_HW_14] = 0; break;           
            case N_LED_MIDI_15:
              setLed_595(N_LED_HW_15, HIGH); leds_que_titilan[N_LED_HW_15] = 0; break;            // Encender el LED correspondiente              
            default: break;  
          }
        }
        else if (led_vel > 0 && led_vel <= VELOCITY_LIM_TITILA)     // Si la velocity es mayor a cero, y menor a LIMITE,
          switch(led_number){
            case N_LED_MIDI_0:
              leds_que_titilan[N_LED_HW_0] = 1; break;      // Encender el LED correspondiente y hacer que titile
            case N_LED_MIDI_1:
              leds_que_titilan[N_LED_HW_1] = 1; break;            
            case N_LED_MIDI_2:
              leds_que_titilan[N_LED_HW_2] = 1; break;            
            case N_LED_MIDI_3:
              leds_que_titilan[N_LED_HW_3] = 1; break;            
            case N_LED_MIDI_4:
              leds_que_titilan[N_LED_HW_4] = 1; break;            
            case N_LED_MIDI_5:
              leds_que_titilan[N_LED_HW_5] = 1; break;            
            case N_LED_MIDI_6:
              leds_que_titilan[N_LED_HW_6] = 1; break;            
            case N_LED_MIDI_7:
              leds_que_titilan[N_LED_HW_7] = 1; break;            
            case N_LED_MIDI_8:
              leds_que_titilan[N_LED_HW_8] = 1; break;            
            case N_LED_MIDI_9:
              leds_que_titilan[N_LED_HW_9] = 1; break;            
            case N_LED_MIDI_10:
              leds_que_titilan[N_LED_HW_10] = 1; break;           
            case N_LED_MIDI_11:
              leds_que_titilan[N_LED_HW_11] = 1; break;           
            case N_LED_MIDI_12:
              leds_que_titilan[N_LED_HW_12] = 1; break;           
            case N_LED_MIDI_13:
              leds_que_titilan[N_LED_HW_13] = 1; break;           
            case N_LED_MIDI_14:
              leds_que_titilan[N_LED_HW_14] = 1; break;           
            case N_LED_MIDI_15:
              leds_que_titilan[N_LED_HW_15] = 1; break;            // Encender el LED correspondiente              
            default: break;  
          }          
        else {                                                      // Si las anteriores no se cumplen, entonces es velocity = 0, es decir NoteOff,
          switch(led_number){
            case N_LED_MIDI_0:
              setLed_595(N_LED_HW_0, LOW); leds_que_titilan[N_LED_HW_0] = 0; break;      // Encender el LED correspondiente y no dejar que titile
            case N_LED_MIDI_1:
              setLed_595(N_LED_HW_1, LOW); leds_que_titilan[N_LED_HW_1] = 0; break;            
            case N_LED_MIDI_2:
              setLed_595(N_LED_HW_2, LOW); leds_que_titilan[N_LED_HW_2] = 0; break;            
            case N_LED_MIDI_3:
              setLed_595(N_LED_HW_3, LOW); leds_que_titilan[N_LED_HW_3] = 0; break;            
            case N_LED_MIDI_4:
              setLed_595(N_LED_HW_4, LOW); leds_que_titilan[N_LED_HW_4] = 0; break;            
            case N_LED_MIDI_5:
              setLed_595(N_LED_HW_5, LOW); leds_que_titilan[N_LED_HW_5] = 0; break;            
            case N_LED_MIDI_6:
              setLed_595(N_LED_HW_6, LOW); leds_que_titilan[N_LED_HW_6] = 0; break;            
            case N_LED_MIDI_7:
              setLed_595(N_LED_HW_7, LOW); leds_que_titilan[N_LED_HW_7] = 0; break;            
            case N_LED_MIDI_8:
              setLed_595(N_LED_HW_8, LOW); leds_que_titilan[N_LED_HW_8] = 0; break;            
            case N_LED_MIDI_9:
              setLed_595(N_LED_HW_9, LOW); leds_que_titilan[N_LED_HW_9] = 0; break;            
            case N_LED_MIDI_10:
              setLed_595(N_LED_HW_10, LOW); leds_que_titilan[N_LED_HW_10] = 0; break;           
            case N_LED_MIDI_11:
              setLed_595(N_LED_HW_11, LOW); leds_que_titilan[N_LED_HW_11] = 0; break;           
            case N_LED_MIDI_12:
              setLed_595(N_LED_HW_12, LOW); leds_que_titilan[N_LED_HW_12] = 0; break;           
            case N_LED_MIDI_13:
              setLed_595(N_LED_HW_13, LOW); leds_que_titilan[N_LED_HW_13] = 0; break;           
            case N_LED_MIDI_14:
              setLed_595(N_LED_HW_14, LOW); leds_que_titilan[N_LED_HW_14] = 0; break;           
            case N_LED_MIDI_15:
              setLed_595(N_LED_HW_15, LOW); leds_que_titilan[N_LED_HW_15] = 0; break;            // Encender el LED correspondiente              
            default: break;  
          }
        }
        break;
      default:
        break;
    }
  }
  // FIN COMENTARIO ///////////////////////////////////////////////////////////////////////////////////////////
}
#endif

#ifdef COMUNICACION_SERIAL
void encender_leds_serial(void){
// EL DEBUG FUNCIONA ENVIANDO DESDE EL TERMINAL SERIE UN NUMERO DEL 0-9 O UNA LETRA DE a-f O DE A-F (10-15) QUE CORRESPONDE AL LED QUE QUEREMOS QUE CAMBIE DE ESTADO
  // CADA VEZ QUE LLEGA EL NUMERO, SE CAMBIA DE UN ESTADO AL SIGUIENTE
  // APAGADO -> TITILANDO -> ENCENDIDO -> APAGADO

  // DESCOMENTAR PARA DEBUGGEAR CON SERIAL ///////////////////////////////////////////////////////////////////////
    static unsigned int leds[NUM_LEDS] = {0,0,0,0,0,0,0,0,0,0,0,0,0,0,0,0};
    if (Serial.available()){                // ¿Llegó un mensaje Serial?
  
      byte led_number = Serial.read();  // Capturo la nota
      switch(led_number){
        case 'a': led_number = 10; break; case 'A': led_number = 10; break;
        case 'b': led_number = 11; break; case 'B': led_number = 11; break;
        case 'c': led_number = 12; break; case 'C': led_number = 12; break;
        case 'd': led_number = 13; break; case 'D': led_number = 13; break;
        case 'e': led_number = 14; break; case 'E': led_number = 14; break;
        case 'f': led_number = 15; break; case 'F': led_number = 15; break;
        case 'o': 
          for (int i = 0; i<NUM_LEDS; i++){
            setLed_595(i, HIGH);
          }
          delay(1000);
          for (int i = 0; i<NUM_LEDS; i++){
            setLed_595(i, LOW);
          }
          return;
        break;
        default: led_number %= 16; break;
      }
      leds[led_number]++;
      leds[led_number] %= 3;
      if (leds[led_number] == 0){
        setLed_595(led_number, LOW);                                // Apagar el LED correspondiente
        leds_que_titilan[led_number] = 0;                         // Actualizar el flag para que no titile más
        Serial.print("LED "); Serial.print(led_number); Serial.println(" apagado.");
      }
      else if (leds[led_number] == 1){
        leds_que_titilan[led_number] = 1;                         // Actualizar el flag para que titile
        Serial.print("LED "); Serial.print(led_number); Serial.println(" titilando.");
      }
      else if (leds[led_number] == 2){
        setLed_595(led_number, HIGH);                               // Encender el LED correspondiente
        leds_que_titilan[led_number] = 0;                         // Actualizar el flag para que no titile más
        Serial.print("LED "); Serial.print(led_number); Serial.println(" encendido.");
      }
  
    }
  // FIN COMENTARIO DEBUG ///////////////////////////////////////////////////////////////////////////////////////////
}
#endif

// Esta función actualiza el estado de los LEDs que titilan
void titilarLeds(void) {
  unsigned int i = 0;
  for (i = 0; i < NUM_LEDS; i++) {                   // Recorrer todos los LEDs
    anteriorMillis = millis();                     // Actualizo el contador de ms usado en la comparación
    if (leds_que_titilan[i]) {                        // Si corresponde titilar este LED,
      if (tiempo_on) {                                   // Y estaba encendido,
        setLed_595(i, HIGH);                               // Se apaga
      }
      else {                                           // Si estaba apagado,
        setLed_595(i, LOW);                              // Se enciende
      }
    }
  }
  tiempo_on = !tiempo_on;
}

#ifdef COMUNICACION_MIDI
void enviarNoteMidi(unsigned int nota, unsigned int veloc) {
  switch (nota) {
    case NOTA_0_HW:  MIDI.sendNoteOn(NOTA_0_MIDI, veloc, CANAL_MIDI_NOTES); break;
    case NOTA_1_HW:  MIDI.sendNoteOn(NOTA_1_MIDI, veloc, CANAL_MIDI_NOTES); break;
    case NOTA_2_HW:  MIDI.sendNoteOn(NOTA_2_MIDI, veloc, CANAL_MIDI_NOTES); break;
    case NOTA_3_HW:  MIDI.sendNoteOn(NOTA_3_MIDI, veloc, CANAL_MIDI_NOTES);  break;
    case NOTA_4_HW:  MIDI.sendNoteOn(NOTA_4_MIDI, veloc, CANAL_MIDI_NOTES);  break;
    case NOTA_5_HW:  MIDI.sendNoteOn(NOTA_5_MIDI, veloc, CANAL_MIDI_NOTES);  break;
    case NOTA_6_HW:  MIDI.sendNoteOn(NOTA_6_MIDI, veloc, CANAL_MIDI_NOTES);  break;                        // MAPEO DE ORDEN DE BOTONES, SEGÚN COMO QUEDARON LOS BOTONES EN HARDWARE Y COMO LOS QUEREMOS EN SOFTWARE
    case NOTA_7_HW:  MIDI.sendNoteOn(NOTA_7_MIDI, veloc, CANAL_MIDI_NOTES);  break;                        // case NRO_BOTON_HARDWARE: MIDI.sendNoteOn(NRO_BOTON_SOFTWARE, velocity, canal);
    case NOTA_8_HW:  MIDI.sendNoteOn(NOTA_8_MIDI, veloc, CANAL_MIDI_NOTES);  break;
    case NOTA_9_HW:  MIDI.sendNoteOn(NOTA_9_MIDI, veloc, CANAL_MIDI_NOTES);  break;
    case NOTA_10_HW:  MIDI.sendNoteOn(NOTA_10_MIDI, veloc, CANAL_MIDI_NOTES);  break;
    case NOTA_11_HW:  MIDI.sendNoteOn(NOTA_11_MIDI, veloc, CANAL_MIDI_NOTES);  break;
    case NOTA_12_HW:  MIDI.sendNoteOn(NOTA_12_MIDI, veloc, CANAL_MIDI_NOTES);  break;
    case NOTA_13_HW:  MIDI.sendNoteOn(NOTA_13_MIDI, veloc, CANAL_MIDI_NOTES);  break;
    case NOTA_14_HW:  MIDI.sendNoteOn(NOTA_14_MIDI, veloc, CANAL_MIDI_NOTES);  break;
    case NOTA_15_HW:  MIDI.sendNoteOn(NOTA_15_MIDI, veloc, CANAL_MIDI_NOTES);  break;
  }
  return;
}
#endif

#ifdef COMUNICACION_SERIAL
void enviarNoteSerial(unsigned int nota, unsigned int veloc) {
// FIN COMENTARIO ///////////////////////////////////////////////////////////////////////////////////////////
  // DEBUG ///////////////////////////////////////////////////////////////////////////////////////////////////////////
  veloc /= 127;
  switch (nota) {
    case NOTA_0_HW:  Serial.print("BOTON NOTE ON"); Serial.print("  Nota: "); Serial.print(NOTA_0_MIDI); Serial.print("  Velocity: "); Serial.println(veloc); break;
    case NOTA_1_HW:  Serial.print("BOTON NOTE ON"); Serial.print("  Nota: "); Serial.print(NOTA_1_MIDI); Serial.print("  Velocity: "); Serial.println(veloc); break;
    case NOTA_2_HW:  Serial.print("BOTON NOTE ON"); Serial.print("  Nota: "); Serial.print(NOTA_2_MIDI); Serial.print("  Velocity: "); Serial.println(veloc); break;
    case NOTA_3_HW:  Serial.print("BOTON NOTE ON"); Serial.print("  Nota: "); Serial.print(NOTA_3_MIDI); Serial.print("  Velocity: "); Serial.println(veloc); break;
    case NOTA_4_HW:  Serial.print("BOTON NOTE ON"); Serial.print("  Nota: "); Serial.print(NOTA_4_MIDI); Serial.print("  Velocity: "); Serial.println(veloc); break;
    case NOTA_5_HW:  Serial.print("BOTON NOTE ON"); Serial.print("  Nota: "); Serial.print(NOTA_5_MIDI); Serial.print("  Velocity: "); Serial.println(veloc); break;
    case NOTA_6_HW:  Serial.print("BOTON NOTE ON"); Serial.print("  Nota: "); Serial.print(NOTA_6_MIDI); Serial.print("  Velocity: "); Serial.println(veloc); break;
    case NOTA_7_HW:  Serial.print("BOTON NOTE ON"); Serial.print("  Nota: "); Serial.print(NOTA_7_MIDI); Serial.print("  Velocity: "); Serial.println(veloc); break;
    case NOTA_8_HW:  Serial.print("BOTON NOTE ON"); Serial.print("  Nota: "); Serial.print(NOTA_8_MIDI); Serial.print("  Velocity: "); Serial.println(veloc); break;
    case NOTA_9_HW:  Serial.print("BOTON NOTE ON"); Serial.print("  Nota: "); Serial.print(NOTA_9_MIDI); Serial.print("  Velocity: "); Serial.println(veloc); break;
    case NOTA_10_HW:  Serial.print("BOTON NOTE ON"); Serial.print("  Nota: "); Serial.print(NOTA_10_MIDI); Serial.print("  Velocity: "); Serial.println(veloc); break;
    case NOTA_11_HW:  Serial.print("BOTON NOTE ON"); Serial.print("  Nota: "); Serial.print(NOTA_11_MIDI); Serial.print("  Velocity: "); Serial.println(veloc); break;
    case NOTA_12_HW:  Serial.print("BOTON NOTE ON"); Serial.print("  Nota: "); Serial.print(NOTA_12_MIDI); Serial.print("  Velocity: "); Serial.println(veloc); break;
    case NOTA_13_HW:  Serial.print("BOTON NOTE ON"); Serial.print("  Nota: "); Serial.print(NOTA_13_MIDI); Serial.print("  Velocity: "); Serial.println(veloc); break;
    case NOTA_14_HW:  Serial.print("BOTON NOTE ON"); Serial.print("  Nota: "); Serial.print(NOTA_14_MIDI); Serial.print("  Velocity: "); Serial.println(veloc); break;
    case NOTA_15_HW:  Serial.print("BOTON NOTE ON"); Serial.print("  Nota: "); Serial.print(NOTA_15_MIDI); Serial.print("  Velocity: "); Serial.println(veloc); break;
  }
  /////// FIN CODIGO DEBUG ////////////////////////////////////////////////////////////////////////////////////////////////
}  
#endif

#ifdef COMUNICACION_MIDI
// Remapea las entradas analógicas y las envía por MIDI
void enviarControlChangeMidi(unsigned int nota) {
  switch (nota) {
    case CC_0_HW:  MIDI.sendControlChange(CC_0_MIDI, velocity[mux][canal], CANAL_MIDI_CC); break;
    case CC_1_HW:  MIDI.sendControlChange(CC_1_MIDI, velocity[mux][canal], CANAL_MIDI_CC); break;
    case CC_2_HW:  MIDI.sendControlChange(CC_2_MIDI, velocity[mux][canal], CANAL_MIDI_CC); break;
    case CC_3_HW:  MIDI.sendControlChange(CC_3_MIDI, velocity[mux][canal], CANAL_MIDI_CC);  break;
    case CC_4_HW:  MIDI.sendControlChange(CC_4_MIDI, velocity[mux][canal], CANAL_MIDI_CC);  break;   
    case CC_5_HW:  MIDI.sendControlChange(CC_5_MIDI, velocity[mux][canal], CANAL_MIDI_CC);  break;
    case CC_6_HW:  MIDI.sendControlChange(CC_6_MIDI, velocity[mux][canal], CANAL_MIDI_CC);  break; // MAPEO DE ORDEN DE ENTRADAS ANALOGICAS, SEGÚN COMO QUEDARON EN HARDWARE
    case CC_7_HW:  MIDI.sendControlChange(CC_7_MIDI, velocity[mux][canal], CANAL_MIDI_CC);  break; // Y COMO LOS QUEREMOS EN SOFTWARE
    case CC_8_HW:  MIDI.sendControlChange(CC_8_MIDI, velocity[mux][canal], CANAL_MIDI_CC);  break; // case NRO_BOTON_HARDWARE: MIDI.sendControlChange(NRO_ANALOG_MIDI, velocity, canal);
    case CC_9_HW:  MIDI.sendControlChange(CC_9_MIDI, velocity[mux][canal], CANAL_MIDI_CC);  break;
    case CC_10_HW:  MIDI.sendControlChange(CC_10_MIDI, velocity[mux][canal], CANAL_MIDI_CC);  break;
    case CC_11_HW:  MIDI.sendControlChange(CC_11_MIDI, velocity[mux][canal], CANAL_MIDI_CC);  break;    
    case CC_12_HW:  MIDI.sendControlChange(CC_12_MIDI, velocity[mux][canal], CANAL_MIDI_CC);  break;    
    case CC_13_HW:  MIDI.sendControlChange(CC_13_MIDI, velocity[mux][canal], CANAL_MIDI_CC);  break;  
    case CC_14_HW:  MIDI.sendControlChange(CC_14_MIDI, velocity[mux][canal], CANAL_MIDI_CC);  break;
    case CC_15_HW:  MIDI.sendControlChange(CC_15_MIDI, velocity[mux][canal], CANAL_MIDI_CC);  break;
    
  }
  return;
}
#endif

#ifdef COMUNICACION_SERIAL
void enviarControlChangeSerial(unsigned int nota) {
  switch (nota) {
    case CC_0_HW:  Serial.print("Numero de pote: "); Serial.print(CC_0_MIDI); Serial.print("  Valor: "); Serial.println(velocity[mux][canal]); break;
    case CC_1_HW:  Serial.print("Numero de pote: "); Serial.print(CC_1_MIDI); Serial.print("  Valor: "); Serial.println(velocity[mux][canal]); break;
    case CC_2_HW:  Serial.print("Numero de pote: "); Serial.print(CC_2_MIDI); Serial.print("  Valor: "); Serial.println(velocity[mux][canal]); break;
    case CC_3_HW:  Serial.print("Numero de pote: "); Serial.print(CC_3_MIDI); Serial.print("  Valor: "); Serial.println(velocity[mux][canal]); break;
    case CC_4_HW:  Serial.print("Numero de pote: "); Serial.print(CC_4_MIDI); Serial.print("  Valor: "); Serial.println(velocity[mux][canal]); break;
    case CC_5_HW:  Serial.print("Numero de pote: "); Serial.print(CC_5_MIDI); Serial.print("  Valor: "); Serial.println(velocity[mux][canal]); break;
    case CC_6_HW:  Serial.print("Numero de pote: "); Serial.print(CC_6_MIDI); Serial.print("  Valor: "); Serial.println(velocity[mux][canal]); break;
    case CC_7_HW:  Serial.print("Numero de pote: "); Serial.print(CC_7_MIDI); Serial.print("  Valor: "); Serial.println(velocity[mux][canal]); break;
    case CC_8_HW:  Serial.print("Numero de pote: "); Serial.print(CC_8_MIDI); Serial.print("  Valor: "); Serial.println(velocity[mux][canal]); break;
    case CC_9_HW:  Serial.print("Numero de pote: "); Serial.print(CC_9_MIDI); Serial.print("  Valor: "); Serial.println(velocity[mux][canal]); break;
    case CC_10_HW:  Serial.print("Numero de pote: "); Serial.print(CC_10_MIDI); Serial.print("  Valor: "); Serial.println(velocity[mux][canal]); break;
    case CC_11_HW:  Serial.print("Numero de pote: "); Serial.print(CC_11_MIDI); Serial.print("  Valor: "); Serial.println(velocity[mux][canal]); break;
    case CC_12_HW:  Serial.print("Numero de pote: "); Serial.print(CC_12_MIDI); Serial.print("  Valor: "); Serial.println(velocity[mux][canal]); break;
    case CC_13_HW:  Serial.print("Numero de pote: "); Serial.print(CC_13_MIDI); Serial.print("  Valor: "); Serial.println(velocity[mux][canal]); break;
    case CC_14_HW:  Serial.print("Numero de pote: "); Serial.print(CC_14_MIDI); Serial.print("  Valor: "); Serial.println(velocity[mux][canal]); break;
    case CC_15_HW:  Serial.print("Numero de pote: "); Serial.print(CC_15_MIDI); Serial.print("  Valor: "); Serial.println(velocity[mux][canal]); break;
  }
  return; 
}
#endif

// Funcion para filtrar el ruido analógico de los pontenciómetros. Guarda 3 valores para detectar si el valor crece o decrece intencionalmente, o si
// es ruido de inestabilidad que baila entre dos valores +-1.
unsigned int esRuido(unsigned int nota) {
  static unsigned int prev2[NUM_CANALES_MUX] = {0, 0, 0, 0, 0, 0, 0, 0, 0, 0, 0, 0, 0, 0, 0, 0};
  if ((velocity[mux][nota] > velocityPrev[mux][nota] + UMBRAL_RUIDO) || (velocity[mux][nota] < velocityPrev[mux][nota] - UMBRAL_RUIDO)) {
    return 0;
  }
  else if ((velocity[mux][nota] == velocityPrev[mux][nota] + UMBRAL_RUIDO) || (velocity[mux][nota] == velocityPrev[mux][nota] - UMBRAL_RUIDO)) {
    if (prev2[nota] == velocity[mux][nota]) {
      return 1;
    }
    else {
      prev2[nota] = velocityPrev[mux][nota];
      return 0;
    }
  }
  else return 1;
}

// Prender o apagar un solo led
void setLed_595(int num_led, int estado) {
  registros[num_led] = estado;
  writeRegisters();
}

// Apagar todos los LEDs
void clearRegisters() {
  for (int i = NUM_LEDS - 1; i >=  0; i--) {
    registros[i] = LOW;
  }
}

// Actualizar el registro de desplazamiento. Actualiza el estado de los LEDs
// Antes de llamar a ésta función, el array 'registros' debería contener el estado requerido para TODOS los LEDs
void writeRegisters() {
  digitalWrite(latchPin, LOW);                  // Se baja la línea de latch para avisar al 595 que se van a enviar datos

  for (int i = NUM_LEDS - 1; i >=  0; i--) {    // Se recorren todos los LEDs,
    digitalWrite(clockPin, LOW);                  // Se baja "manualmente" la línea de clock

    int val = registros[i];                       // Se recupera el estado del LED

    digitalWrite(dataPin, val);                   // Se escribe el estado del LED en la línea de datos
    digitalWrite(clockPin, HIGH);                 // Se levanta la línea de clock para el próximo bit
  }
  digitalWrite(latchPin, HIGH);                 // Se vuelve a poner en HIGH la línea de latch para avisar que no se enviarán mas datos
}
